// Logisim project sqrt2.circ as structural Verilog
module main (
  input  ENABLE,
  input  [15:0] IO_DATA_IN,
  output NAN,
  output PINF,
  output NINF,
  output RESULT,
  output [15:0] IO_DATA_OUT
);

  wire CLK_out;

  Clock CLK (.out(CLK_out));
  sqrt sqrt_1 (
    .CLK(CLK_out), .ENABLE(ENABLE), .IO_DATA_IN(IO_DATA_IN), .IS_NAN(NAN), .IS_PINF(PINF), .IS_NINF(NINF),
    .RESULT(RESULT), .IO_DATA_OUT(IO_DATA_OUT));
endmodule

module sqrt (
  input  CLK,
  input  ENABLE,
  input  [15:0] IO_DATA_IN,
  output IS_NAN,
  output IS_PINF,
  output IS_NINF,
  output RESULT,
  output [15:0] IO_DATA_OUT
);

  wire input_parser_1_is_inf, input_parser_1_is_nan, input_parser_1_is_zero, input_parser_1_sign;
  wire [15:0] memory_16bits_1_val, special_case_handler_1_special_out;

  clk_counter clk_counter_1 (.CLK(CLK), .ENABLE(ENABLE), .VAL(IO_DATA_IN[7:0]));
  // Probe on memory_16bits_1_val
  memory_16bits memory_16bits_1 (.DATA(IO_DATA_IN), .ENABLE(ENABLE), .VAL(memory_16bits_1_val));  // open: C
  input_parser input_parser_1 (
    .N(memory_16bits_1_val), .Sign(input_parser_1_sign), .IS_ZERO(input_parser_1_is_zero),
    .IS_NAN(input_parser_1_is_nan), .IS_INF(input_parser_1_is_inf));  // open: Mant, Exp
  exp_mantissa_preparer exp_mantissa_preparer_1 ();  // open: MANT, EXP, IS_DENORM_INP, M_ADJ, E_HALF_BIASED
  // Probe on special_case_handler_1_special_out
  special_case_handler special_case_handler_1 (
    .Sign(input_parser_1_sign), .IS_ZERO_INP(input_parser_1_is_zero), .IS_NAN_INP(input_parser_1_is_nan),
    .IS_INF_INP(input_parser_1_is_inf), .SPECIAL_OUT(special_case_handler_1_special_out), .IS_PINF(IS_PINF),
    .IS_NAN(IS_NAN), .IS_NINF(IS_NINF), .BYPASS_CORE(RESULT));

  assign IO_DATA_OUT = IO_DATA_IN;
endmodule

module sum1 (
  input  A,
  input  B,
  input  Cin,
  output S,
  output Cout
);

  wire and_1_out, and_2_out, xor_1_out;

  xor xor_1 (xor_1_out, A, B);
  xor xor_2 (S, xor_1_out, Cin);
  and and_1 (and_1_out, xor_1_out, Cin);
  and and_2 (and_2_out, A, B);
  or or_1 (Cout, and_1_out, and_2_out);
endmodule

module sum2 (
  input  [1:0] A,
  input  [1:0] B,
  input  Cin,
  output [1:0] S,
  output Cout
);

  wire sum1_1_cout;

  sum1 sum1_1 (.A(A[0]), .B(B[0]), .Cin(Cin), .S(S[0]), .Cout(sum1_1_cout));
  sum1 sum1_2 (.A(A[1]), .B(B[1]), .Cin(sum1_1_cout), .S(S[1]), .Cout(Cout));
endmodule

module sum4 (
  input  [3:0] A,
  input  [3:0] B,
  input  Cin,
  output [3:0] S,
  output Cout
);

  wire sum2_1_cout;

  sum2 sum2_1 (.A(A[1:0]), .B(B[1:0]), .Cin(Cin), .S(S[1:0]), .Cout(sum2_1_cout));
  sum2 sum2_2 (.A(A[3:2]), .B(B[3:2]), .Cin(sum2_1_cout), .S(S[3:2]), .Cout(Cout));

  // Other names for the same wires on the sheet: A1[1:0] = A[3:2]; B1[1:0] = B[3:2]
endmodule

module sum8 (
  input  [7:0] A,
  input  [7:0] B,
  input  Cin,
  output [7:0] S,
  output Cout
);

  wire sum4_1_cout;

  sum4 sum4_1 (.A(A[3:0]), .B(B[3:0]), .Cin(Cin), .S(S[3:0]), .Cout(sum4_1_cout));
  sum4 sum4_2 (.A(A[7:4]), .B(B[7:4]), .Cin(sum4_1_cout), .S(S[7:4]), .Cout(Cout));

  // Other names for the same wires on the sheet: A1[3:0] = A[7:4]; B1[3:0] = B[7:4]
endmodule

module sum16 (
  input  [15:0] A,
  input  [15:0] B,
  input  Cin,
  output [15:0] S,
  output Cout
);

  wire sum8_1_cout;

  sum8 sum8_1 (.A(A[7:0]), .B(B[7:0]), .Cin(Cin), .S(S[7:0]), .Cout(sum8_1_cout));
  sum8 sum8_2 (.A(A[15:8]), .B(B[15:8]), .Cin(sum8_1_cout), .S(S[15:8]), .Cout(Cout));

  // Other names for the same wires on the sheet: A1[7:0] = A[15:8]; B1[7:0] = B[15:8]
endmodule

module sum32 (
  input  [31:0] A,
  input  [31:0] B,
  input  Cin,
  output [31:0] S,
  output Cout
);

  wire sum16_1_cout;

  sum16 sum16_1 (.A(A[15:0]), .B(B[15:0]), .Cin(Cin), .S(S[15:0]), .Cout(sum16_1_cout));
  sum16 sum16_2 (.A(A[31:16]), .B(B[31:16]), .Cin(sum16_1_cout), .S(S[31:16]), .Cout(Cout));

  // Other names for the same wires on the sheet: A1[15:0] = A[31:16]; B1[15:0] = B[31:16]
endmodule

module input_parser (
  input  [15:0] N,
  output [9:0] Mant,
  output [4:0] Exp,
  output Sign,
  output IS_ZERO,
  output IS_NAN,
  output IS_INF
);

  wire IS_EXP_0, IS_EXP_MAX, M_0, M_NOT_0;

  nor nor_1 (M_0, N[0], N[1], N[2], N[3], N[4], N[5], N[6], N[7], N[8], N[9]);
  not not_1 (M_NOT_0, M_0);
  nor nor_2 (IS_EXP_0, N[10], N[11], N[12], N[13], N[14]);
  and and_1 (IS_EXP_MAX, N[10], N[11], N[12], N[13], N[14]);
  // Probe on IS_EXP_0
  // Probe on IS_EXP_MAX
  and and_2 (IS_ZERO, IS_EXP_0, M_0);
  and and_3 (IS_NAN, M_NOT_0, IS_EXP_MAX);
  and and_4 (IS_INF, M_0, IS_EXP_MAX);

  assign Exp = N[14:10];
  assign Mant = N[9:0];
  assign Sign = N[15];
endmodule

module right_shift (
  input  [31:0] in_1,
  output OutBit,
  output [31:0] Res
);


  assign OutBit = in_1[0];
  assign Res = {1'b0, in_1[31:1]};
endmodule

module left_shift (
  input  [31:0] in_1,
  output [31:0] Res,
  output OutBit
);


  assign OutBit = in_1[31];
  assign Res = {in_1[30:0], 1'b0};
endmodule

module special_case_handler (
  input  Sign,
  input  IS_ZERO_INP,
  input  IS_NAN_INP,
  input  IS_INF_INP,
  output [15:0] SPECIAL_OUT,
  output IS_PINF,
  output IS_NAN,
  output IS_NINF,
  output BYPASS_CORE
);

  wire and_1_out, and_2_out, and_3_out, not_1_out, not_2_out, not_3_out;

  not not_1 (not_1_out, IS_ZERO_INP);
  and and_1 (and_1_out, Sign, not_1_out);
  not not_2 (not_2_out, IS_ZERO_INP);
  not not_3 (not_3_out, Sign);
  and and_2 (and_2_out, Sign, not_2_out);
  and and_3 (and_3_out, Sign, IS_INF_INP);
  and and_4 (IS_PINF, not_3_out, IS_INF_INP);
  or or_1 (IS_NAN, and_2_out, and_3_out, IS_NAN_INP);
  or or_2 (BYPASS_CORE, and_1_out, IS_ZERO_INP, IS_NAN_INP, IS_INF_INP);
  mux_4to1_16bit mux_4to1_16bit_1 (
    .D2(16'hfd00), .D1(16'h7c00), .D0({Sign, {15{1'b0}}}), .S0(IS_PINF), .S1(IS_NAN), .RES(SPECIAL_OUT));  // open: D3

  assign IS_NINF = 1'b0;
endmodule

module mux_2to1_1bit (
  input  D1,
  input  D0,
  input  COND,
  output RES
);

  wire and_1_out, and_2_out, not_1_out;

  not not_1 (not_1_out, COND);
  and and_1 (and_1_out, D1, COND);
  and and_2 (and_2_out, D0, not_1_out);
  or or_1 (RES, and_1_out, and_2_out);
endmodule

module mux_4to1_1bit (
  input  D3,
  input  D2,
  input  D1,
  input  D0,
  input  S0,
  input  S1,
  output RES
);

  wire mux_2to1_1bit_1_res, mux_2to1_1bit_2_res;

  mux_2to1_1bit mux_2to1_1bit_1 (.D1(D3), .D0(D2), .COND(S0), .RES(mux_2to1_1bit_1_res));
  mux_2to1_1bit mux_2to1_1bit_2 (.D1(D1), .D0(D0), .COND(S0), .RES(mux_2to1_1bit_2_res));
  mux_2to1_1bit mux_2to1_1bit_3 (.D1(mux_2to1_1bit_1_res), .D0(mux_2to1_1bit_2_res), .COND(S1), .RES(RES));
endmodule

module mux_8to1_1bit (
  input  D7,
  input  D6,
  input  D5,
  input  D4,
  input  D3,
  input  D2,
  input  D1,
  input  D0,
  input  S0,
  input  S1,
  input  S2,
  output RES
);

  wire mux_4to1_1bit_1_res, mux_4to1_1bit_2_res;

  mux_4to1_1bit mux_4to1_1bit_1 (.D3(D7), .D2(D6), .D1(D5), .D0(D4), .S0(S0), .S1(S1), .RES(mux_4to1_1bit_1_res));
  mux_4to1_1bit mux_4to1_1bit_2 (.D3(D3), .D2(D2), .D1(D1), .D0(D0), .S0(S0), .S1(S1), .RES(mux_4to1_1bit_2_res));
  mux_2to1_1bit mux_2to1_1bit_1 (.D1(mux_4to1_1bit_1_res), .D0(mux_4to1_1bit_2_res), .COND(S2), .RES(RES));
endmodule

module mux_2to1_16bit (
  input  [15:0] D1,
  input  [15:0] D0,
  input  COND,
  output [15:0] RES
);

  wire [15:0] and_1_out, and_2_out;
  wire [15:15] not_1_out;

  not not_1 (not_1_out[15], COND);
  assign and_1_out = D1 & {16{COND}};  // AND_Gate and_1, 16 bits wide
  assign and_2_out = D0 & {16{not_1_out[15]}};  // AND_Gate and_2, 16 bits wide
  assign RES = and_1_out | and_2_out;  // OR_Gate or_1, 16 bits wide
endmodule

module mux_4to1_16bit (
  input  [15:0] D3,
  input  [15:0] D2,
  input  [15:0] D1,
  input  [15:0] D0,
  input  S0,
  input  S1,
  output [15:0] RES
);

  wire [15:0] mux_2to1_16bit_1_res, mux_2to1_16bit_2_res;

  mux_2to1_16bit mux_2to1_16bit_1 (.D1(D3), .D0(D2), .COND(S0), .RES(mux_2to1_16bit_1_res));
  mux_2to1_16bit mux_2to1_16bit_2 (.D1(D1), .D0(D0), .COND(S0), .RES(mux_2to1_16bit_2_res));
  mux_2to1_16bit mux_2to1_16bit_3 (.D1(mux_2to1_16bit_1_res), .D0(mux_2to1_16bit_2_res), .COND(S1), .RES(RES));
endmodule

module exp_mantissa_preparer (
  input  [9:0] MANT,
  input  [4:0] EXP,
  input  IS_DENORM_INP,
  output [11:0] M_ADJ,
  output [7:0] E_HALF_BIASED
);

  wire not_1_out;
  wire [15:0] mux_2to1_16bit_1_res;

  not not_1 (not_1_out, EXP[0]);
  // Probe on {EXP[4:1], 1'b1}
  // Probe on 8'h8
  // Probe on mux_2to1_16bit_1_res
  mux_2to1_16bit mux_2to1_16bit_1 (
    .D1({{5{1'b0}}, MANT, 1'b0}), .D0({{6{1'b0}}, MANT}), .COND(not_1_out), .RES(mux_2to1_16bit_1_res));
  // Probe on E_HALF_BIASED
  sum8 sum8_1 (.A({3'b000, EXP[4:1], 1'b1}), .B(8'h8), .S(E_HALF_BIASED));  // open: Cin, Cout
endmodule

module rs_trigger_sync (
  input  R,
  input  C,
  input  S,
  output Q,
  output NOT_Q
);

  wire and_1_out, and_2_out;

  and and_1 (and_1_out, R, C);
  and and_2 (and_2_out, C, S);
  nor nor_1 (Q, and_1_out, NOT_Q);
  nor nor_2 (NOT_Q, Q, and_2_out);
endmodule

module d_trigger (
  input  D,
  input  C,
  output Q,
  output NOT_Q
);

  wire not_1_out;

  not not_1 (not_1_out, D);
  rs_trigger_sync rs_trigger_sync_1 (.R(not_1_out), .C(C), .S(D), .Q(Q), .NOT_Q(NOT_Q));
endmodule

module d_trigger_front (
  input  D,
  input  C,
  output Q,
  output NOT_Q
);

  wire d_trigger_1_q, not_1_out;

  not not_1 (not_1_out, C);
  d_trigger d_trigger_1 (.D(D), .C(not_1_out), .Q(d_trigger_1_q));  // open: NOT_Q
  d_trigger d_trigger_2 (.D(d_trigger_1_q), .C(C), .Q(Q), .NOT_Q(NOT_Q));
endmodule

module memory_2bits (
  input  [1:0] DATA,
  input  C,
  input  ENABLE,
  output [1:0] VAL
);

  d_trigger_enbl_front d_trigger_enbl_front_1 (.D(DATA[0]), .C(C), .ENABLE(ENABLE), .Q(VAL[0]));  // open: NOT_Q
  d_trigger_enbl_front d_trigger_enbl_front_2 (.D(DATA[1]), .C(C), .ENABLE(ENABLE), .Q(VAL[1]));  // open: NOT_Q
endmodule

module memory_4bits (
  input  [3:0] DATA,
  input  C,
  input  ENABLE,
  output [3:0] VAL
);

  memory_2bits memory_2bits_1 (.DATA(DATA[1:0]), .C(C), .ENABLE(ENABLE), .VAL(VAL[1:0]));
  memory_2bits memory_2bits_2 (.DATA(DATA[3:2]), .C(C), .ENABLE(ENABLE), .VAL(VAL[3:2]));
endmodule

module memory_8bits (
  input  [7:0] DATA,
  input  C,
  input  ENABLE,
  output [7:0] VAL
);

  memory_4bits memory_4bits_1 (.DATA(DATA[3:0]), .C(C), .ENABLE(ENABLE), .VAL(VAL[3:0]));
  memory_4bits memory_4bits_2 (.DATA(DATA[7:4]), .C(C), .ENABLE(ENABLE), .VAL(VAL[7:4]));
endmodule

module memory_16bits (
  input  [15:0] DATA,
  input  C,
  input  ENABLE,
  output [15:0] VAL
);

  memory_8bits memory_8bits_1 (.DATA(DATA[7:0]), .C(C), .ENABLE(ENABLE), .VAL(VAL[7:0]));
  memory_8bits memory_8bits_2 (.DATA(DATA[15:8]), .C(C), .ENABLE(ENABLE), .VAL(VAL[15:8]));
endmodule

module memory_32bits (
  input  [31:0] DATA,
  input  C,
  input  ENABLE,
  output [31:0] VAL
);

  memory_16bits memory_16bits_1 (.DATA(DATA[15:0]), .C(C), .ENABLE(ENABLE), .VAL(VAL[15:0]));
  memory_16bits memory_16bits_2 (.DATA(DATA[31:16]), .C(C), .ENABLE(ENABLE), .VAL(VAL[31:16]));
endmodule

module clk_counter (
  input  CLK,
  input  ENABLE,
  output [7:0] VAL
);

  wire [7:0] sum8_1_s;

  // Probe on VAL
  memory_8bits memory_8bits_1 (.DATA(sum8_1_s), .C(CLK), .ENABLE(ENABLE), .VAL(VAL));
  sum8 sum8_1 (.A(VAL), .B(8'h1), .S(sum8_1_s));  // open: Cin, Cout
  // Probe on sum8_1_s
endmodule

module rs_trigger_sync_enable (
  input  R,
  input  C,
  input  S,
  input  ENABLE,
  output Q,
  output NOT_Q
);

  wire and_1_out, not_1_out, not_2_out, or_1_out, or_2_out;

  or or_1 (or_1_out, R, not_1_out);
  not not_1 (not_1_out, ENABLE);
  or or_2 (or_2_out, C, not_2_out);
  not not_2 (not_2_out, ENABLE);
  and and_1 (and_1_out, S, ENABLE);
  rs_trigger_sync rs_trigger_sync_1 (.R(or_1_out), .C(or_2_out), .S(and_1_out), .Q(Q), .NOT_Q(NOT_Q));
endmodule

module d_trigger_enbl (
  input  D,
  input  C,
  input  ENABLE,
  output Q,
  output NOT_Q
);

  wire not_1_out;

  not not_1 (not_1_out, D);
  rs_trigger_sync_enable rs_trigger_sync_enable_1 (.R(not_1_out), .C(C), .S(D), .ENABLE(ENABLE), .Q(Q), .NOT_Q(NOT_Q));
endmodule

module d_trigger_enbl_front (
  input  D,
  input  C,
  input  ENABLE,
  output Q,
  output NOT_Q
);

  wire d_trigger_enbl_1_q, not_1_out;

  not not_1 (not_1_out, C);
  d_trigger_enbl d_trigger_enbl_1 (.D(D), .C(not_1_out), .ENABLE(ENABLE), .Q(d_trigger_enbl_1_q));  // open: NOT_Q
  d_trigger_enbl d_trigger_enbl_2 (.D(d_trigger_enbl_1_q), .C(C), .ENABLE(ENABLE), .Q(Q), .NOT_Q(NOT_Q));
endmodule
